// Logisim project trabalho_todo.circ as structural Verilog: 6 circuits, main circuit Banco_de_Registradores
module Banco_de_Registradores (
  input  [2:0] R_ADR,
  input  [31:0] RD,
  input  WR,
  input  [2:0] RS1_I,
  input  [2:0] RS2_I,
  input  CLK,
  output [31:0] RS1_O,
  output [31:0] RS2_O
);

  wire demultiplexer_1_out0, demultiplexer_1_out1, demultiplexer_1_out2, demultiplexer_1_out3,
       demultiplexer_1_out4, demultiplexer_1_out5, demultiplexer_1_out6, demultiplexer_1_out7;
  wire [31:0] X0_q, X1_q, X2_q, X3_q, X4_q, X5_q, X6_q, X7_q;

  Demultiplexer #(.select(3)) demultiplexer_1 (
    .out0(demultiplexer_1_out0), .out1(demultiplexer_1_out1), .out2(demultiplexer_1_out2),
    .out3(demultiplexer_1_out3), .out4(demultiplexer_1_out4), .out5(demultiplexer_1_out5),
    .out6(demultiplexer_1_out6), .out7(demultiplexer_1_out7), .in(WR), .sel(R_ADR));
  Register #(.width(32)) X0 (.D(RD), .en(demultiplexer_1_out7), .clk(CLK), .Q(X0_q));  // open: clr
  Register #(.width(32)) X1 (.D(RD), .en(demultiplexer_1_out6), .clk(CLK), .Q(X1_q));  // open: clr
  Register #(.width(32)) X2 (.D(RD), .en(demultiplexer_1_out5), .clk(CLK), .Q(X2_q));  // open: clr
  Register #(.width(32)) X3 (.D(RD), .en(demultiplexer_1_out4), .clk(CLK), .Q(X3_q));  // open: clr
  Register #(.width(32)) X4 (.D(RD), .en(demultiplexer_1_out3), .clk(CLK), .Q(X4_q));  // open: clr
  Register #(.width(32)) X5 (.D(RD), .en(demultiplexer_1_out2), .clk(CLK), .Q(X5_q));  // open: clr
  Register #(.width(32)) X6 (.D(RD), .en(demultiplexer_1_out1), .clk(CLK), .Q(X6_q));  // open: clr
  Register #(.width(32)) X7 (.D(RD), .en(demultiplexer_1_out0), .clk(CLK), .Q(X7_q));  // open: clr
  Multiplexer #(.select(3), .width(32)) multiplexer_1 (
    .in0(X0_q), .in1(X1_q), .in2(X2_q), .in3(X3_q), .in4(X4_q), .in5(X5_q), .in6(X6_q), .in7(X7_q),
    .out(RS1_O), .sel(RS1_I));
  Multiplexer #(.select(3), .width(32)) multiplexer_2 (
    .in0(X0_q), .in1(X1_q), .in2(X2_q), .in3(X3_q), .in4(X4_q), .in5(X5_q), .in6(X6_q), .in7(X7_q),
    .out(RS2_O), .sel(RS2_I));
endmodule

module main (
);

  wire [23:0] banco_de_registradores_1_p1;
  wire [31:0] banco_de_registradores_1_p4, banco_de_registradores_1_p5, multiplexer_1_out,
       processador_de_imm_1_o;

  Unidade_de_Controle unidade_de_controle_1 (.OPCODE(banco_de_registradores_1_p1[4:0]));  // open: RD, ULA_or_MEM, ALU_R_or_IMM, MR, WR, JUMP, BRANCH, MW, ALU_OP
  // Banco_de_Registradores banco_de_registradores_1: pin names not known; wires that end beside it: banco_de_registradores_1_p1, banco_de_registradores_1_p1, banco_de_registradores_1_p1, banco_de_registradores_1_p4, banco_de_registradores_1_p5
  Processador_de_IMM processador_de_imm_1 (.I(banco_de_registradores_1_p1), .O(processador_de_imm_1_o));
  Multiplexer #(.width(32)) multiplexer_1 (
    .in0(banco_de_registradores_1_p5), .in1(processador_de_imm_1_o), .out(multiplexer_1_out));  // open: sel
  ULA ula_1 (.RS1(banco_de_registradores_1_p4), .RS2(multiplexer_1_out));  // open: OP_ULA, ULA_O
  // Pins of 5 and 24 bits meet at banco_de_registradores_1_p1
endmodule

module ULA (
  input  [2:0] OP_ULA,
  input  [31:0] RS1,
  input  [31:0] RS2,
  output [31:0] ULA_O
);

  wire [31:0] adder_1_out, divider_1_out, multiplier_1_out, shifter_1_out, shifter_2_out, subtractor_1_out;

  Adder #(.width(32)) adder_1 (.a(RS2), .b(RS1), .out(adder_1_out));  // open: cin, cout
  Subtractor #(.width(32)) subtractor_1 (.a(RS2), .b(RS1), .out(subtractor_1_out));  // open: bin, bout
  Multiplier #(.width(32)) multiplier_1 (.a(RS2), .b(RS1), .out(multiplier_1_out));  // open: cin, cout
  Divider #(.width(32)) divider_1 (.a(RS2), .b(RS1), .out(divider_1_out));  // open: upper, rem
  Shifter #(.width(32)) shifter_1 (.in(RS1), .\dist (RS2[4:0]), .out(shifter_1_out));
  Shifter #(.shift("lr"), .width(32)) shifter_2 (.in(RS1), .\dist (RS2[4:0]), .out(shifter_2_out));
  Multiplexer #(.select(3), .width(32)) multiplexer_1 (
    .in0(adder_1_out), .in1(subtractor_1_out), .in2(multiplier_1_out), .in3(divider_1_out),
    .in4(shifter_1_out), .in5(shifter_2_out), .out(ULA_O), .sel(OP_ULA));  // open: in6, in7
endmodule

module Unidade_de_Controle (
  input  [4:0] OPCODE,
  output RD,
  output ULA_or_MEM,
  output ALU_R_or_IMM,
  output MR,
  output WR,
  output JUMP,
  output BRANCH,
  output MW,
  output [3:0] ALU_OP
);

  ROM #(.addrWidth(5), .dataWidth(12)) rom_1 (
    .addr(OPCODE), .data({ALU_OP, MW, JUMP, BRANCH, MR, WR, ULA_or_MEM, ALU_R_or_IMM, RD}));
endmodule

module Processador_de_IMM (
  input  [23:0] I,
  output [31:0] O
);

  wire [23:0] demultiplexer_1_out0, demultiplexer_1_out1, demultiplexer_1_out2;
  wire [31:0] bit_extender_1_out, bit_extender_2_out, bit_extender_3_out;

  Demultiplexer #(.select(2), .width(24)) demultiplexer_1 (
    .out0(demultiplexer_1_out0), .out1(demultiplexer_1_out1), .out2(demultiplexer_1_out2), .in(I));  // open: out3, sel
  assign bit_extender_1_out = {{23{demultiplexer_1_out0[23]}}, demultiplexer_1_out0[23:15]};  // Bit_Extender bit_extender_1
  assign bit_extender_2_out = {{28{demultiplexer_1_out1[23]}}, demultiplexer_1_out1[23:20]};  // Bit_Extender bit_extender_2
  assign bit_extender_3_out = {{18{demultiplexer_1_out2[23]}}, demultiplexer_1_out2[23:10]};  // Bit_Extender bit_extender_3
  Multiplexer #(.select(2), .width(32)) multiplexer_1 (
    .in0(bit_extender_1_out), .in1(bit_extender_2_out), .in2(bit_extender_3_out), .out(O));  // open: in3, sel

  // Notes on the sheet:
  //   Tipo R & B
  //   Tipo S
  //   Tipo J
endmodule

module MD (
  input  [2:0] INPUT_PC
);

  ROM #(.addrWidth(3), .dataWidth(24)) rom_1 (.addr(INPUT_PC));  // open: data
endmodule
